// Logisim project 8_bit_cpu.circ as structural Verilog: 2 circuits, main circuit contador
module contador (
  input  Reset,
  output [7:0] out_2
);

  wire Pulso_out;
  wire [7:0] adder_1_out, counter_1_q;

  Clock Pulso (.out(Pulso_out));
  Counter counter_1 (.D(adder_1_out), .Q(counter_1_q), .clk(Pulso_out), .clr(Reset));  // open: load, count, carry, up
  Adder adder_1 (.a(8'h1), .b(counter_1_q), .out(adder_1_out));  // open: cin, cout
  ROM Memoria (.addr(counter_1_q), .data(out_2));

  // Notes on the sheet:
  //   contents of Memoria (hex, n*v repeats v):
  //   ff 43*0 11 1 11
endmodule

module registradores (
  input  [2:0] read_register_3,
  input  [2:0] read_register_2,
  input  [7:0] write_data,
  input  [2:0] write_register,
  input  register_write,
  input  reset,
  output [7:0] read_data_1,
  output [7:0] read_data_2
);

  wire clock_pulse_out, WE0, WE1, WE2, WE3, WE4, WE5, WE6, WE7;
  wire [7:0] demultiplexer_2_out0, demultiplexer_2_out1, demultiplexer_2_out2, demultiplexer_2_out3,
       demultiplexer_2_out4, demultiplexer_2_out5, demultiplexer_2_out6, demultiplexer_2_out7, Reg0, Reg1,
       Reg2, Reg3, Reg4, Reg5, Reg6, Reg7;

  Clock clock_pulse (.out(clock_pulse_out));
  Demultiplexer #(.select(3)) demultiplexer_1 (
    .out0(WE0), .out1(WE1), .out2(WE2), .out3(WE3), .out4(WE4), .out5(WE5), .out6(WE6), .out7(WE7),
    .in(register_write), .sel(write_register));
  Demultiplexer #(.select(3), .width(8)) demultiplexer_2 (
    .out0(demultiplexer_2_out0), .out1(demultiplexer_2_out1), .out2(demultiplexer_2_out2),
    .out3(demultiplexer_2_out3), .out4(demultiplexer_2_out4), .out5(demultiplexer_2_out5),
    .out6(demultiplexer_2_out6), .out7(demultiplexer_2_out7), .in(write_data), .sel(write_register));
  Register reg_0 (.D(demultiplexer_2_out0), .en(WE0), .Q(Reg0), .clk(clock_pulse_out), .clr(reset));
  Register reg_1 (.D(demultiplexer_2_out1), .en(WE1), .Q(Reg1), .clk(clock_pulse_out), .clr(reset));
  Register reg_2 (.D(demultiplexer_2_out2), .en(WE2), .Q(Reg2), .clk(clock_pulse_out), .clr(reset));
  Register reg_3 (.D(demultiplexer_2_out3), .en(WE3), .Q(Reg3), .clk(clock_pulse_out), .clr(reset));
  Register reg_4 (.D(demultiplexer_2_out4), .en(WE4), .Q(Reg4), .clk(clock_pulse_out), .clr(reset));
  Register reg_5 (.D(demultiplexer_2_out5), .en(WE5), .Q(Reg5), .clk(clock_pulse_out));  // open: clr
  Register reg_6 (.D(demultiplexer_2_out6), .en(WE6), .Q(Reg6), .clk(clock_pulse_out));  // open: clr
  Register reg_7 (.D(demultiplexer_2_out7), .en(WE7), .Q(Reg7), .clk(clock_pulse_out), .clr(reset));
  Multiplexer #(.select(3), .width(8)) multiplexer_1 (
    .in0(Reg0), .in1(Reg1), .in2(Reg2), .in3(Reg3), .in4(Reg4), .in5(Reg5), .in6(Reg6), .in7(Reg7),
    .out(read_data_1), .sel(read_register_3));
  Multiplexer #(.select(3), .width(8)) multiplexer_2 (
    .in0(Reg0), .in1(Reg1), .in2(Reg2), .in3(Reg3), .in4(Reg4), .in5(Reg5), .in6(Reg6), .in7(Reg7),
    .out(read_data_2), .sel(read_register_2));

  // Other names for the same wires on the sheet: Read1[2:0] = read_register_3; Read2[2:0] = read_register_2
endmodule
